# Fritzing sketch sketch (saved by Fritzing 0.9.3b)
breadboards: 1

parts:
  Part1 = Arduino Uno (Rev3)
  Part2 = Bluetooth HC-05 Macho
  hc-sr1 = hc-sr04
  hc-sr2 = hc-sr04
  Part3 = Arduino Modkit Shield  # not connected
  LCD1 = LCD screen

nets:
  N1: Part1.A0, LCD1.DB4
  N2: Part1.A1, LCD1.DB5
  N3: Part1.A2, LCD1.DB6
  N4: Part1.A3, LCD1.DB7
  N5: Part1.D9_PWM, hc-sr1.Echo
  N6: Part1.D10_PWM/SS, LCD1.RS
  N7: Part1.D12/MISO, LCD1.E
  N8: Part1.D13/SCK, hc-sr2.Echo
  GND: Part1.GND, Part2.GND, hc-sr2.GND, LCD1.VSS, LCD1.LED+
  N9: Part1.D3_PWM, hc-sr1.Trig, hc-sr2.Trig
  N10: Part1.D5_PWM, Part2.RXD
  N11: Part1.D6_PWM, Part2.TXD
  VCC: Part1.5V, Part2.VCC, hc-sr2.VCC, LCD1.VDD, LCD1.LED-
